# Fritzing sketch schematic (saved by Fritzing 0.9.4)
circuit board: 6.55561cm x 7.81795cm
breadboards: 1

parts:
  Raspberry_Pi_Pico = Raspberry Pi Pico
  HC-SR04_Sensor_1 = HC-SR04 Ultrasonic Distance Sensor
  Piezo1 = Piezo Speaker - PC Mount [part_number=COM-07950]
  OLED1 = OLED 128x64 I2C Monochrome Display GND-VDD

nets:
  N1: Raspberry_Pi_Pico.pin_1, OLED1.SDA
  N2: Raspberry_Pi_Pico.pin_2, OLED1.SCK
  GND: Raspberry_Pi_Pico.pin_3, Raspberry_Pi_Pico.pin_8, Raspberry_Pi_Pico.pin_13, Raspberry_Pi_Pico.pin_18, Raspberry_Pi_Pico.pin_23, Raspberry_Pi_Pico.pin_28, Raspberry_Pi_Pico.pin_33, Raspberry_Pi_Pico.pin_38, Raspberry_Pi_Pico.pin_42, HC-SR04_Sensor_1.GND, Piezo1.GND, OLED1.GND
  N3: Raspberry_Pi_Pico.pin_4, HC-SR04_Sensor_1.ECHO
  N4: Raspberry_Pi_Pico.pin_5, HC-SR04_Sensor_1.TRIG
  N5: Raspberry_Pi_Pico.pin_17, Piezo1.VCC
  N6: Raspberry_Pi_Pico.pin_36, OLED1.VDD
  N7: Raspberry_Pi_Pico.pin_40, HC-SR04_Sensor_1.VCC

custom parts:
  Raspberry Pi Pico: Raspberry Pi Pico. Based around the RP2040 microcontroller the Pico is a low cost microcontroller device bringing Raspberry Pi quality, cost, and easy of use to the microcontroller space. Jan 2021, Split part in to two versions: tht (this one) and SMD. This one will drill holes for a .1 in header in pcb to allow plugging in the module as well as providing pads to solder the module to the top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
  Piezo Speaker - PC Mount: This is a small 12mm round speaker that operates around the audible 2kHz range. You can use these speakers to create simple music or user interfaces. Each speaker is PTH solderable and requires an operating voltage of 3.5-5V with a mean current of 35mA max. These speakers also have a typical sound output of 95 dBA and a coil resistance of 42 ±6.3 ohms.
  OLED 128x64 I2C Monochrome Display GND-VDD: OLED 128x64 I2C Monochrome Display. Note: there are two variants of this part, this one is the GND VDD SCK SDA variant. The other is VDD GND SCK SDA. Make sure you select the part that matches your module as using the incorrect part will probably destroy your module! In addition the mounting holes are marked on silkscreen but not by default drilled. If you want drilled mounting holes, copy a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
